# Fritzing sketch Lightsaber (saved by Fritzing 0.9.10b)

parts:
  Adafruit_RP2040_Prop-Maker_Feather1 = Adafruit RP2040 Prop-Maker Feather [part_number=#5768]
  NEOPIXEL1 = Neopixel Strip -- Black (30/m) [part_number=1376]
  NEOPIXEL2 = Neopixel Strip -- Black (30/m) [part_number=1376]
  SP1 = SPEAKER [package=pcb_mount_speaker]
  Part1 = Lithium Ion Battery Pack 3.7V 4400mAh [part_number=354]
  R1 = Rotary Potentiometer (Small) [maximum_resistance=100kΩ knob_status=50% power=0.5W package=THT]
  S1 = Taiway 100-SP-X-T1 SPDT Miniature Toggle Switch [part_number=100-SP-X-T1-0-0-B1-M2 package=THT]
  S2 = Taiway 100-SP-X-T1 SPDT Miniature Toggle Switch [part_number=100-SP-X-T1-0-0-B1-M2 package=THT]
  S3 = Taiway 100-SP-X-T1 SPDT Miniature Toggle Switch [part_number=100-SP-X-T1-0-0-B1-M2 package=THT]
  S4 = Taiway 100-SP-X-T1 SPDT Miniature Toggle Switch [part_number=100-SP-X-T1-0-0-B1-M2 package=THT]
  S5 = Taiway 100-SP-X-T1 SPDT Miniature Toggle Switch [part_number=100-SP-X-T1-0-0-B1-M2 package=THT]
  S6 = Taiway 100-SP-X-T1 SPDT Miniature Toggle Switch [part_number=100-SP-X-T1-0-0-B1-M2 package=THT]
  S7 = Taiway 100-SP-X-T1 SPDT Miniature Toggle Switch [part_number=100-SP-X-T1-0-0-B1-M2 package=THT]
  S8 = Taiway 100-SP-X-T1 SPDT Miniature Toggle Switch [part_number=100-SP-X-T1-0-0-B1-M2 package=THT]
  S10 = Pushbutton [package="[THT]"]
  LED1 = RGB LED (com. anode, rbg) [package="5 mm [THT]"]
  Part2 = Flora Bluefruit LE
  Part3 = 12 NeoPixel Ring [part_number=1643]  # not connected

nets:
  N1: Adafruit_RP2040_Prop-Maker_Feather1.TX, Part2.RXI
  N2: Adafruit_RP2040_Prop-Maker_Feather1.RX, Part2.TXO
  N3: Adafruit_RP2040_Prop-Maker_Feather1.A3, LED1.red_cathode
  N4: Adafruit_RP2040_Prop-Maker_Feather1.A2, LED1.blue_cathode
  N5: Adafruit_RP2040_Prop-Maker_Feather1.A1, LED1.green_cathode
  N6: Adafruit_RP2040_Prop-Maker_Feather1.A0, R1.wiper
  GND: Adafruit_RP2040_Prop-Maker_Feather1.GND, NEOPIXEL1.GND, NEOPIXEL2.GND, Part1.negative, R1.leg1, S1.L1, S2.L1, S3.L1, S4.L1, S5.L1, S6.L1, S7.L1, S8.L1, S10.Pin_1, S10.Pin_2, Part2.GND
  +3V3: Adafruit_RP2040_Prop-Maker_Feather1.+3V3, R1.leg2, LED1.common_anode, Part2.3.3V
  N7: Adafruit_RP2040_Prop-Maker_Feather1.D13, S5.L2
  N8: Adafruit_RP2040_Prop-Maker_Feather1.D12, S6.L2
  N9: Adafruit_RP2040_Prop-Maker_Feather1.D11, S7.L2
  N10: Adafruit_RP2040_Prop-Maker_Feather1.D10, S8.L2
  N11: Adafruit_RP2040_Prop-Maker_Feather1.D9, S1.L2
  N12: Adafruit_RP2040_Prop-Maker_Feather1.D6, S2.L2
  N13: Adafruit_RP2040_Prop-Maker_Feather1.D5, S3.L2
  N14: Adafruit_RP2040_Prop-Maker_Feather1.SCL, S4.L2
  N15: Adafruit_RP2040_Prop-Maker_Feather1.PIXELOUT, NEOPIXEL1.Din, NEOPIXEL2.Din
  +5V: Adafruit_RP2040_Prop-Maker_Feather1.V+, NEOPIXEL1.+5V, NEOPIXEL2.+5V
  N16: Adafruit_RP2040_Prop-Maker_Feather1.BUTTON, S10.Pin_3, S10.Pin_4
  N17: Adafruit_RP2040_Prop-Maker_Feather1.VO-, SP1.+
  N18: Adafruit_RP2040_Prop-Maker_Feather1.VO+, SP1.-
  N19: Adafruit_RP2040_Prop-Maker_Feather1.VBAT, Part1.positive

custom parts:
  Adafruit RP2040 Prop-Maker Feather: The Adafruit Feather series gives you lots of options for a small, portable, rechargeable microcontroller board. By picking a feather and stacking on a FeatherWing you can create advanced projects quickly. One popular combo is our Feather M4 or Feather RP2040 with a Prop-Maker FeatherWing on top to create animatronics or props that boot up instantly and can drive LEDs, and small speakers.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
  Neopixel Strip -- Black (30/m): These NeoPixel strips have 30 digitally-addressable pixel LEDs per meter and are very affordable and are only 12.5 mm wide, 10 mm if you remove the strip from the casing.
  Lithium Ion Battery Pack 3.7V 4400mAh: This lithium ion pack is made of 2 balanced 2200mAh cells for a total of 4400mA capacity! The cells are connected in parallel and spot-welded to a protection circuit that provides over-voltage, under-voltage and over-current protection. Each cell can provide 1A of current for about 4 hours so all together the peak current you can draw is a little over 1.5 Amps. Note that these batteries are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
  Flora Bluefruit LE: Would you like to add powerful and easy-to-use Bluetooth Low Energy to your wearable FLORA project? Heck yeah! With BLE now included in modern smart phones and tablets, its fun to add wireless connectivity. So what you really need is the new Adafruit Flora Bluefruit LE! The Flora Bluefruit LE makes it easy to add Bluetooth Low Energy connectivity to your Flora. Sew 4 traces (or solder 4 wires)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
  12 NeoPixel Ring: 12 ultra bright smart LED NeoPixels are arranged in a circle with 1.5" (37mm) outer diameter. The rings are 'chainable' - connect the output pin of one to the input pin of another. Use only one microcontroller pin to control as many as you can chain together! Each LED is addressable as the driver chip is inside the LED. Each one has ~18mA constant current drive so the color will be very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
